// Logisim project regfile.circ as structural Verilog: 33 circuits, main circuit main
module main (
  input  [4:0] Read_Register_1,
  input  [4:0] Read_Register_2,
  input  [4:0] Write_Register,
  input  [31:0] Write_Data,
  input  Write_Enable,
  input  Clock,
  output [31:0] s0_Value,
  output [31:0] s1_Value,
  output [31:0] s2_Value,
  output [31:0] ra_Value,
  output [31:0] sp_Value,
  output [31:0] Read_Data_1,
  output [31:0] Read_Data_2
);

  wire wr0, wr1, wr2, wr3, wr4, wr5, wr6, wr7, wr8, wr9, wr10, wr11, wr12, wr13, wr14, wr15, wr16, wr17,
       wr18, wr19, wr20, wr21, wr22, wr23, wr24, wr25, wr26, wr27, wr28, wr29, wr30, wr31;
  wire [31:0] _0_r1, _0_r2, _1_r1, _1_r2, _2_r1, _2_r2, _3_r1, _3_r2, _4_r1, _4_r2, _5_r1, _5_r2, _6_r1,
       _6_r2, _7_r1, _7_r2, _8_r1, _8_r2, _9_r1, _9_r2, _10_r1, _10_r2, _11_r1, _11_r2, _12_r1, _12_r2,
       _13_r1, _13_r2, _14_r1, _14_r2, _15_r1, _15_r2, _16_r1, _16_r2, _17_r1, _17_r2, _18_r1, _18_r2,
       _19_r1, _19_r2, _20_r1, _20_r2, _21_r1, _21_r2, _22_r1, _22_r2, _23_r1, _23_r2, _24_r1, _24_r2,
       _25_r1, _25_r2, _26_r1, _26_r2, _27_r1, _27_r2, _28_r1, _28_r2, _29_r1, _29_r2, _30_r1, _30_r2,
       _31_r1, _31_r2, r1_0, r1_1, r1_2, r1_3, r1_4, r1_5, r1_6, r1_7, r1_8, r1_9, r1_10, r1_11, r1_12,
       r1_13, r1_14, r1_15, r1_16, r1_17, r1_18, r1_19, r1_20, r1_21, r1_22, r1_23, r1_24, r1_25, r1_26,
       r1_27, r1_28, r1_29, r1_30, r1_31, r2_0, r2_1, r2_2, r2_3, r2_4, r2_5, r2_6, r2_7, r2_8, r2_9, r2_10,
       r2_11, r2_12, r2_13, r2_14, r2_15, r2_16, r2_17, r2_18, r2_19, r2_20, r2_21, r2_22, r2_23, r2_24,
       r2_25, r2_26, r2_27, r2_28, r2_29, r2_30, r2_31;

  Multiplexer #(.select(5), .width(32), .enable("false")) multiplexer_1 (
    .in0(_0_r1), .in1(_1_r1), .in2(_2_r1), .in3(_3_r1), .in4(_4_r1), .in5(_5_r1), .in6(_6_r1), .in7(_7_r1),
    .in8(_8_r1), .in9(_9_r1), .in10(_10_r1), .in11(_11_r1), .in12(_12_r1), .in13(_13_r1), .in14(_14_r1),
    .in15(_15_r1), .in16(_16_r1), .in17(_17_r1), .in18(_18_r1), .in19(_19_r1), .in20(_20_r1), .in21(_21_r1),
    .in22(_22_r1), .in23(_23_r1), .in24(_24_r1), .in25(_25_r1), .in26(_26_r1), .in27(_27_r1), .in28(_28_r1),
    .in29(_29_r1), .in30(_30_r1), .in31(_31_r1), .out(Read_Data_1), .sel(Read_Register_1));
  Multiplexer #(.select(5), .width(32), .enable("false")) multiplexer_2 (
    .in0(_0_r2), .in1(_1_r2), .in2(_2_r2), .in3(_3_r2), .in4(_4_r2), .in5(_5_r2), .in6(_6_r2), .in7(_7_r2),
    .in8(_8_r2), .in9(_9_r2), .in10(_10_r2), .in11(_11_r2), .in12(_12_r2), .in13(_13_r2), .in14(_14_r2),
    .in15(_15_r2), .in16(_16_r2), .in17(_17_r2), .in18(_18_r2), .in19(_19_r2), .in20(_20_r2), .in21(_21_r2),
    .in22(_22_r2), .in23(_23_r2), .in24(_24_r2), .in25(_25_r2), .in26(_26_r2), .in27(_27_r2), .in28(_28_r2),
    .in29(_29_r2), .in30(_30_r2), .in31(_31_r2), .out(Read_Data_2), .sel(Read_Register_2));
  Decoder #(.select(5), .enable("false")) decoder_1 (
    .out0(wr0), .out1(wr1), .out2(wr2), .out3(wr3), .out4(wr4), .out5(wr5), .out6(wr6), .out7(wr7),
    .out8(wr8), .out9(wr9), .out10(wr10), .out11(wr11), .out12(wr12), .out13(wr13), .out14(wr14),
    .out15(wr15), .out16(wr16), .out17(wr17), .out18(wr18), .out19(wr19), .out20(wr20), .out21(wr21),
    .out22(wr22), .out23(wr23), .out24(wr24), .out25(wr25), .out26(wr26), .out27(wr27), .out28(wr28),
    .out29(wr29), .out30(wr30), .out31(wr31), .sel(Write_Register));
  R0 r0_1 (
    .read1_r_num(r1_0), .write_data(Write_Data), .write_r_num(wr0), .write_en(1'b0), .read2_r_num(r2_0),
    .clk(Clock), .read1_data(_0_r1), .read2_data(_0_r2));
  R1 u_r1_1 (
    .read1_r_num(r1_1), .write_data(Write_Data), .write_r_num(wr1), .write_en(Write_Enable),
    .read2_r_num(r2_1), .clk(Clock), .read1_data(_1_r1), .read2_data(_1_r2));
  R2 u_r2_1 (
    .read1_r_num(r1_2), .write_data(Write_Data), .write_r_num(wr2), .write_en(Write_Enable),
    .read2_r_num(r2_2), .clk(Clock), .read1_data(_2_r1), .read2_data(_2_r2));
  R3 r3_1 (
    .read1_r_num(r1_3), .write_data(Write_Data), .write_r_num(wr3), .write_en(Write_Enable),
    .read2_r_num(r2_3), .clk(Clock), .read1_data(_3_r1), .read2_data(_3_r2));
  R4 r4_1 (
    .read1_r_num(r1_4), .write_data(Write_Data), .write_r_num(wr4), .write_en(Write_Enable),
    .read2_r_num(r2_4), .clk(Clock), .read1_data(_4_r1), .read2_data(_4_r2));
  R5 r5_1 (
    .read1_r_num(r1_5), .write_data(Write_Data), .write_r_num(wr5), .write_en(Write_Enable),
    .read2_r_num(r2_5), .clk(Clock), .read1_data(_5_r1), .read2_data(_5_r2));
  R6 r6_1 (
    .read1_r_num(r1_6), .write_data(Write_Data), .write_r_num(wr6), .write_en(Write_Enable),
    .read2_r_num(r2_6), .clk(Clock), .read1_data(_6_r1), .read2_data(_6_r2));
  R7 r7_1 (
    .read1_r_num(r1_7), .write_data(Write_Data), .write_r_num(wr7), .write_en(Write_Enable),
    .read2_r_num(r2_7), .clk(Clock), .read1_data(_7_r1), .read2_data(_7_r2));
  Demultiplexer #(.select(5), .width(32), .enable("false")) demultiplexer_1 (
    .out0(r1_0), .out1(r1_1), .out2(r1_2), .out3(r1_3), .out4(r1_4), .out5(r1_5), .out6(r1_6), .out7(r1_7),
    .out8(r1_8), .out9(r1_9), .out10(r1_10), .out11(r1_11), .out12(r1_12), .out13(r1_13), .out14(r1_14),
    .out15(r1_15), .out16(r1_16), .out17(r1_17), .out18(r1_18), .out19(r1_19), .out20(r1_20), .out21(r1_21),
    .out22(r1_22), .out23(r1_23), .out24(r1_24), .out25(r1_25), .out26(r1_26), .out27(r1_27), .out28(r1_28),
    .out29(r1_29), .out30(r1_30), .out31(r1_31), .in({32{1'b1}}), .sel(Read_Register_1));
  R8 r8_1 (
    .read1_r_num(r1_8), .write_data(Write_Data), .write_r_num(wr8), .write_en(Write_Enable),
    .read2_r_num(r2_8), .clk(Clock), .read1_data(_8_r1), .read2_data(_8_r2));
  R9 r9_1 (
    .read1_r_num(r1_9), .write_data(Write_Data), .write_r_num(wr9), .write_en(Write_Enable),
    .read2_r_num(r2_9), .clk(Clock), .read1_data(_9_r1), .read2_data(_9_r2));
  R10 r10_1 (
    .read1_r_num(r1_10), .write_data(Write_Data), .write_r_num(wr10), .write_en(Write_Enable),
    .read2_r_num(r2_10), .clk(Clock), .read1_data(_10_r1), .read2_data(_10_r2));
  R11 r11_1 (
    .read1_r_num(r1_11), .write_data(Write_Data), .write_r_num(wr11), .write_en(Write_Enable),
    .read2_r_num(r2_11), .clk(Clock), .read1_data(_11_r1), .read2_data(_11_r2));
  R12 r12_1 (
    .read1_r_num(r1_12), .write_data(Write_Data), .write_r_num(wr12), .write_en(Write_Enable),
    .read2_r_num(r2_12), .clk(Clock), .read1_data(_12_r1), .read2_data(_12_r2));
  R13 r13_1 (
    .read1_r_num(r1_13), .write_data(Write_Data), .write_r_num(wr13), .write_en(Write_Enable),
    .read2_r_num(r2_13), .clk(Clock), .read1_data(_13_r1), .read2_data(_13_r2));
  R14 r14_1 (
    .read1_r_num(r1_14), .write_data(Write_Data), .write_r_num(wr14), .write_en(Write_Enable),
    .read2_r_num(r2_14), .clk(Clock), .read1_data(_14_r1), .read2_data(_14_r2));
  R15 r15_1 (
    .read1_r_num(r1_15), .write_data(Write_Data), .write_r_num(wr15), .write_en(Write_Enable),
    .read2_r_num(r2_15), .clk(Clock), .read1_data(_15_r1), .read2_data(_15_r2));
  Demultiplexer #(.select(5), .width(32), .enable("false")) demultiplexer_2 (
    .out0(r2_0), .out1(r2_1), .out2(r2_2), .out3(r2_3), .out4(r2_4), .out5(r2_5), .out6(r2_6), .out7(r2_7),
    .out8(r2_8), .out9(r2_9), .out10(r2_10), .out11(r2_11), .out12(r2_12), .out13(r2_13), .out14(r2_14),
    .out15(r2_15), .out16(r2_16), .out17(r2_17), .out18(r2_18), .out19(r2_19), .out20(r2_20), .out21(r2_21),
    .out22(r2_22), .out23(r2_23), .out24(r2_24), .out25(r2_25), .out26(r2_26), .out27(r2_27), .out28(r2_28),
    .out29(r2_29), .out30(r2_30), .out31(r2_31), .in({32{1'b1}}), .sel(Read_Register_2));
  R16 r16_1 (
    .read1_r_num(r1_16), .write_data(Write_Data), .write_r_num(wr16), .write_en(Write_Enable),
    .read2_r_num(r2_16), .clk(Clock), .read1_data(_16_r1), .out(s0_Value), .read2_data(_16_r2));
  R17 r17_1 (
    .read1_r_num(r1_17), .write_data(Write_Data), .write_r_num(wr17), .write_en(Write_Enable),
    .read2_r_num(r2_17), .clk(Clock), .read1_data(_17_r1), .out(s1_Value), .read2_data(_17_r2));
  R18 r18_1 (
    .read1_r_num(r1_18), .write_data(Write_Data), .write_r_num(wr18), .write_en(Write_Enable),
    .read2_r_num(r2_18), .clk(Clock), .read1_data(_18_r1), .out(s2_Value), .read2_data(_18_r2));
  R19 r19_1 (
    .read1_r_num(r1_19), .write_data(Write_Data), .write_r_num(wr19), .write_en(Write_Enable),
    .read2_r_num(r2_19), .clk(Clock), .read1_data(_19_r1), .read2_data(_19_r2));
  R20 r20_1 (
    .read1_r_num(r1_20), .write_data(Write_Data), .write_r_num(wr20), .write_en(Write_Enable),
    .read2_r_num(r2_20), .clk(Clock), .read1_data(_20_r1), .read2_data(_20_r2));
  R21 r21_1 (
    .read1_r_num(r1_21), .write_data(Write_Data), .write_r_num(wr21), .write_en(Write_Enable),
    .read2_r_num(r2_21), .clk(Clock), .read1_data(_21_r1), .read2_data(_21_r2));
  R22 r22_1 (
    .read1_r_num(r1_22), .write_data(Write_Data), .write_r_num(wr22), .write_en(Write_Enable),
    .read2_r_num(r2_22), .clk(Clock), .read1_data(_22_r1), .read2_data(_22_r2));
  R23 r23_1 (
    .read1_r_num(r1_23), .write_data(Write_Data), .write_r_num(wr23), .write_en(Write_Enable),
    .read2_r_num(r2_23), .clk(Clock), .read1_data(_23_r1), .read2_data(_23_r2));
  R24 r24_1 (
    .read1_r_num(r1_24), .write_data(Write_Data), .write_r_num(wr24), .write_en(Write_Enable),
    .read2_r_num(r2_24), .clk(Clock), .read1_data(_24_r1), .read2_data(_24_r2));
  R25 r25_1 (
    .read1_r_num(r1_25), .write_data(Write_Data), .write_r_num(wr25), .write_en(Write_Enable),
    .read2_r_num(r2_25), .clk(Clock), .read1_data(_25_r1), .read2_data(_25_r2));
  R26 r26_1 (
    .read1_r_num(r1_26), .write_data(Write_Data), .write_r_num(wr26), .write_en(Write_Enable),
    .read2_r_num(r2_26), .clk(Clock), .read1_data(_26_r1), .read2_data(_26_r2));
  R27 r27_1 (
    .read1_r_num(r1_27), .write_data(Write_Data), .write_r_num(wr27), .write_en(Write_Enable),
    .read2_r_num(r2_27), .clk(Clock), .read1_data(_27_r1), .read2_data(_27_r2));
  R28 r28_1 (
    .read1_r_num(r1_28), .write_data(Write_Data), .write_r_num(wr28), .write_en(Write_Enable),
    .read2_r_num(r2_28), .clk(Clock), .read1_data(_28_r1), .read2_data(_28_r2));
  R29 r29_1 (
    .read1_r_num(r1_29), .write_data(Write_Data), .write_r_num(wr29), .write_en(Write_Enable),
    .read2_r_num(r2_29), .clk(Clock), .read1_data(_29_r1), .out(sp_Value), .read2_data(_29_r2));
  R30 r30_1 (
    .read1_r_num(r1_30), .write_data(Write_Data), .write_r_num(wr30), .write_en(Write_Enable),
    .read2_r_num(r2_30), .clk(Clock), .read1_data(_30_r1), .read2_data(_30_r2));
  R31 r31_1 (
    .read1_r_num(r1_31), .write_data(Write_Data), .write_r_num(wr31), .write_en(Write_Enable),
    .read2_r_num(r2_31), .clk(Clock), .read1_data(_31_r1), .out(ra_Value), .read2_data(_31_r2));

  // Other names for the same wires on the sheet: clk = Clock; ra[31:0] = ra_Value; read_data1[31:0] = Read_Data_1;
  //   read_data2[31:0] = Read_Data_2; read_reg1[4:0] = Read_Register_1; read_reg2[4:0] = Read_Register_2;
  //   s0[31:0] = s0_Value; s1[31:0] = s1_Value; s2[31:0] = s2_Value; sp[31:0] = sp_Value; write_en = Write_Enable;
  //   write_reg[4:0] = Write_Register

  // Notes on the sheet:
  //   INPUTS to your circuit
  //   DON'T CHANGE THE LOCATIONS OF THE INPUTS AND OUTPUTS!
  //   These are DEBUG/TEST outputs from your circuit.
  //   OUTPUTS from your circuit
endmodule

module R0 (
  input  [31:0] read1_r_num,
  input  [31:0] write_data,
  input  write_r_num,
  input  write_en,
  input  clk,
  input  [31:0] read2_r_num,
  output [31:0] read1_data,
  output [31:0] read2_data
);

  wire and_1_out;
  wire [31:0] R0_q;

  and and_1 (and_1_out, write_r_num, write_en);
  Register #(.width(32)) R0 (.D(write_data), .en(and_1_out), .Q(R0_q), .clk(clk));  // open: clr
  assign read1_data = read1_r_num & R0_q;  // AND_Gate and_2, 32 bits wide
  assign read2_data = R0_q & read2_r_num;  // AND_Gate and_3, 32 bits wide
endmodule

module R1 (
  input  [31:0] read1_r_num,
  input  [31:0] write_data,
  input  write_r_num,
  input  write_en,
  input  clk,
  input  [31:0] read2_r_num,
  output [31:0] read1_data,
  output [31:0] read2_data
);

  wire and_1_out;
  wire [31:0] R1_q;

  and and_1 (and_1_out, write_r_num, write_en);
  Register #(.width(32)) R1 (.D(write_data), .en(and_1_out), .Q(R1_q), .clk(clk));  // open: clr
  assign read1_data = read1_r_num & R1_q;  // AND_Gate and_2, 32 bits wide
  assign read2_data = R1_q & read2_r_num;  // AND_Gate and_3, 32 bits wide
endmodule

module R2 (
  input  [31:0] read1_r_num,
  input  [31:0] write_data,
  input  write_r_num,
  input  write_en,
  input  clk,
  input  [31:0] read2_r_num,
  output [31:0] read1_data,
  output [31:0] read2_data
);

  wire and_1_out;
  wire [31:0] R2_q;

  and and_1 (and_1_out, write_r_num, write_en);
  Register #(.width(32)) R2 (.D(write_data), .en(and_1_out), .Q(R2_q), .clk(clk));  // open: clr
  assign read1_data = read1_r_num & R2_q;  // AND_Gate and_2, 32 bits wide
  assign read2_data = R2_q & read2_r_num;  // AND_Gate and_3, 32 bits wide
endmodule

module R3 (
  input  [31:0] read1_r_num,
  input  [31:0] write_data,
  input  write_r_num,
  input  write_en,
  input  clk,
  input  [31:0] read2_r_num,
  output [31:0] read1_data,
  output [31:0] read2_data
);

  wire and_1_out;
  wire [31:0] R3_q;

  and and_1 (and_1_out, write_r_num, write_en);
  Register #(.width(32)) R3 (.D(write_data), .en(and_1_out), .Q(R3_q), .clk(clk));  // open: clr
  assign read1_data = read1_r_num & R3_q;  // AND_Gate and_2, 32 bits wide
  assign read2_data = R3_q & read2_r_num;  // AND_Gate and_3, 32 bits wide
endmodule

module R4 (
  input  [31:0] read1_r_num,
  input  [31:0] write_data,
  input  write_r_num,
  input  write_en,
  input  clk,
  input  [31:0] read2_r_num,
  output [31:0] read1_data,
  output [31:0] read2_data
);

  wire and_1_out;
  wire [31:0] R4_q;

  and and_1 (and_1_out, write_r_num, write_en);
  Register #(.width(32)) R4 (.D(write_data), .en(and_1_out), .Q(R4_q), .clk(clk));  // open: clr
  assign read1_data = read1_r_num & R4_q;  // AND_Gate and_2, 32 bits wide
  assign read2_data = R4_q & read2_r_num;  // AND_Gate and_3, 32 bits wide
endmodule

module R5 (
  input  [31:0] read1_r_num,
  input  [31:0] write_data,
  input  write_r_num,
  input  write_en,
  input  clk,
  input  [31:0] read2_r_num,
  output [31:0] read1_data,
  output [31:0] read2_data
);

  wire and_1_out;
  wire [31:0] R5_q;

  and and_1 (and_1_out, write_r_num, write_en);
  Register #(.width(32)) R5 (.D(write_data), .en(and_1_out), .Q(R5_q), .clk(clk));  // open: clr
  assign read1_data = read1_r_num & R5_q;  // AND_Gate and_2, 32 bits wide
  assign read2_data = R5_q & read2_r_num;  // AND_Gate and_3, 32 bits wide
endmodule

module R6 (
  input  [31:0] read1_r_num,
  input  [31:0] write_data,
  input  write_r_num,
  input  write_en,
  input  clk,
  input  [31:0] read2_r_num,
  output [31:0] read1_data,
  output [31:0] read2_data
);

  wire and_1_out;
  wire [31:0] R6_q;

  and and_1 (and_1_out, write_r_num, write_en);
  Register #(.width(32)) R6 (.D(write_data), .en(and_1_out), .Q(R6_q), .clk(clk));  // open: clr
  assign read1_data = read1_r_num & R6_q;  // AND_Gate and_2, 32 bits wide
  assign read2_data = R6_q & read2_r_num;  // AND_Gate and_3, 32 bits wide
endmodule

module R7 (
  input  [31:0] read1_r_num,
  input  [31:0] write_data,
  input  write_r_num,
  input  write_en,
  input  clk,
  input  [31:0] read2_r_num,
  output [31:0] read1_data,
  output [31:0] read2_data
);

  wire and_1_out;
  wire [31:0] R7_q;

  and and_1 (and_1_out, write_r_num, write_en);
  Register #(.width(32)) R7 (.D(write_data), .en(and_1_out), .Q(R7_q), .clk(clk));  // open: clr
  assign read1_data = read1_r_num & R7_q;  // AND_Gate and_2, 32 bits wide
  assign read2_data = R7_q & read2_r_num;  // AND_Gate and_3, 32 bits wide
endmodule

module R8 (
  input  [31:0] read1_r_num,
  input  [31:0] write_data,
  input  write_r_num,
  input  write_en,
  input  clk,
  input  [31:0] read2_r_num,
  output [31:0] read1_data,
  output [31:0] read2_data
);

  wire and_1_out;
  wire [31:0] R8_q;

  and and_1 (and_1_out, write_r_num, write_en);
  Register #(.width(32)) R8 (.D(write_data), .en(and_1_out), .Q(R8_q), .clk(clk));  // open: clr
  assign read1_data = read1_r_num & R8_q;  // AND_Gate and_2, 32 bits wide
  assign read2_data = R8_q & read2_r_num;  // AND_Gate and_3, 32 bits wide
endmodule

module R9 (
  input  [31:0] read1_r_num,
  input  [31:0] write_data,
  input  write_r_num,
  input  write_en,
  input  clk,
  input  [31:0] read2_r_num,
  output [31:0] read1_data,
  output [31:0] read2_data
);

  wire and_1_out;
  wire [31:0] R9_q;

  and and_1 (and_1_out, write_r_num, write_en);
  Register #(.width(32)) R9 (.D(write_data), .en(and_1_out), .Q(R9_q), .clk(clk));  // open: clr
  assign read1_data = read1_r_num & R9_q;  // AND_Gate and_2, 32 bits wide
  assign read2_data = R9_q & read2_r_num;  // AND_Gate and_3, 32 bits wide
endmodule

module R10 (
  input  [31:0] read1_r_num,
  input  [31:0] write_data,
  input  write_r_num,
  input  write_en,
  input  clk,
  input  [31:0] read2_r_num,
  output [31:0] read1_data,
  output [31:0] read2_data
);

  wire and_1_out;
  wire [31:0] R10_q;

  and and_1 (and_1_out, write_r_num, write_en);
  Register #(.width(32)) R10 (.D(write_data), .en(and_1_out), .Q(R10_q), .clk(clk));  // open: clr
  assign read1_data = read1_r_num & R10_q;  // AND_Gate and_2, 32 bits wide
  assign read2_data = R10_q & read2_r_num;  // AND_Gate and_3, 32 bits wide
endmodule

module R11 (
  input  [31:0] read1_r_num,
  input  [31:0] write_data,
  input  write_r_num,
  input  write_en,
  input  clk,
  input  [31:0] read2_r_num,
  output [31:0] read1_data,
  output [31:0] read2_data
);

  wire and_1_out;
  wire [31:0] R11_q;

  and and_1 (and_1_out, write_r_num, write_en);
  Register #(.width(32)) R11 (.D(write_data), .en(and_1_out), .Q(R11_q), .clk(clk));  // open: clr
  assign read1_data = read1_r_num & R11_q;  // AND_Gate and_2, 32 bits wide
  assign read2_data = R11_q & read2_r_num;  // AND_Gate and_3, 32 bits wide
endmodule

module R12 (
  input  [31:0] read1_r_num,
  input  [31:0] write_data,
  input  write_r_num,
  input  write_en,
  input  clk,
  input  [31:0] read2_r_num,
  output [31:0] read1_data,
  output [31:0] read2_data
);

  wire and_1_out;
  wire [31:0] R12_q;

  and and_1 (and_1_out, write_r_num, write_en);
  Register #(.width(32)) R12 (.D(write_data), .en(and_1_out), .Q(R12_q), .clk(clk));  // open: clr
  assign read1_data = read1_r_num & R12_q;  // AND_Gate and_2, 32 bits wide
  assign read2_data = R12_q & read2_r_num;  // AND_Gate and_3, 32 bits wide
endmodule

module R13 (
  input  [31:0] read1_r_num,
  input  [31:0] write_data,
  input  write_r_num,
  input  write_en,
  input  clk,
  input  [31:0] read2_r_num,
  output [31:0] read1_data,
  output [31:0] read2_data
);

  wire and_1_out;
  wire [31:0] R13_q;

  and and_1 (and_1_out, write_r_num, write_en);
  Register #(.width(32)) R13 (.D(write_data), .en(and_1_out), .Q(R13_q), .clk(clk));  // open: clr
  assign read1_data = read1_r_num & R13_q;  // AND_Gate and_2, 32 bits wide
  assign read2_data = R13_q & read2_r_num;  // AND_Gate and_3, 32 bits wide
endmodule

module R14 (
  input  [31:0] read1_r_num,
  input  [31:0] write_data,
  input  write_r_num,
  input  write_en,
  input  clk,
  input  [31:0] read2_r_num,
  output [31:0] read1_data,
  output [31:0] read2_data
);

  wire and_1_out;
  wire [31:0] R14_q;

  and and_1 (and_1_out, write_r_num, write_en);
  Register #(.width(32)) R14 (.D(write_data), .en(and_1_out), .Q(R14_q), .clk(clk));  // open: clr
  assign read1_data = read1_r_num & R14_q;  // AND_Gate and_2, 32 bits wide
  assign read2_data = R14_q & read2_r_num;  // AND_Gate and_3, 32 bits wide
endmodule

module R15 (
  input  [31:0] read1_r_num,
  input  [31:0] write_data,
  input  write_r_num,
  input  write_en,
  input  clk,
  input  [31:0] read2_r_num,
  output [31:0] read1_data,
  output [31:0] read2_data
);

  wire and_1_out;
  wire [31:0] R15_q;

  and and_1 (and_1_out, write_r_num, write_en);
  Register #(.width(32)) R15 (.D(write_data), .en(and_1_out), .Q(R15_q), .clk(clk));  // open: clr
  assign read1_data = read1_r_num & R15_q;  // AND_Gate and_2, 32 bits wide
  assign read2_data = R15_q & read2_r_num;  // AND_Gate and_3, 32 bits wide
endmodule

module R16 (
  input  [31:0] read1_r_num,
  input  [31:0] write_data,
  input  write_r_num,
  input  write_en,
  input  clk,
  input  [31:0] read2_r_num,
  output [31:0] read1_data,
  output [31:0] out,
  output [31:0] read2_data
);

  wire and_1_out;

  and and_1 (and_1_out, write_r_num, write_en);
  Register #(.width(32)) R16 (.D(write_data), .en(and_1_out), .Q(out), .clk(clk));  // open: clr
  assign read1_data = read1_r_num & out;  // AND_Gate and_2, 32 bits wide
  assign read2_data = out & read2_r_num;  // AND_Gate and_3, 32 bits wide
endmodule

module R17 (
  input  [31:0] read1_r_num,
  input  [31:0] write_data,
  input  write_r_num,
  input  write_en,
  input  clk,
  input  [31:0] read2_r_num,
  output [31:0] read1_data,
  output [31:0] out,
  output [31:0] read2_data
);

  wire and_1_out;

  and and_1 (and_1_out, write_r_num, write_en);
  Register #(.width(32)) R17 (.D(write_data), .en(and_1_out), .Q(out), .clk(clk));  // open: clr
  assign read1_data = read1_r_num & out;  // AND_Gate and_2, 32 bits wide
  assign read2_data = out & read2_r_num;  // AND_Gate and_3, 32 bits wide
endmodule

module R18 (
  input  [31:0] read1_r_num,
  input  [31:0] write_data,
  input  write_r_num,
  input  write_en,
  input  clk,
  input  [31:0] read2_r_num,
  output [31:0] read1_data,
  output [31:0] out,
  output [31:0] read2_data
);

  wire and_1_out;

  and and_1 (and_1_out, write_r_num, write_en);
  Register #(.width(32)) R18 (.D(write_data), .en(and_1_out), .Q(out), .clk(clk));  // open: clr
  assign read1_data = read1_r_num & out;  // AND_Gate and_2, 32 bits wide
  assign read2_data = out & read2_r_num;  // AND_Gate and_3, 32 bits wide
endmodule

module R19 (
  input  [31:0] read1_r_num,
  input  [31:0] write_data,
  input  write_r_num,
  input  write_en,
  input  clk,
  input  [31:0] read2_r_num,
  output [31:0] read1_data,
  output [31:0] read2_data
);

  wire and_1_out;
  wire [31:0] R19_q;

  and and_1 (and_1_out, write_r_num, write_en);
  Register #(.width(32)) R19 (.D(write_data), .en(and_1_out), .Q(R19_q), .clk(clk));  // open: clr
  assign read1_data = read1_r_num & R19_q;  // AND_Gate and_2, 32 bits wide
  assign read2_data = R19_q & read2_r_num;  // AND_Gate and_3, 32 bits wide
endmodule

module R20 (
  input  [31:0] read1_r_num,
  input  [31:0] write_data,
  input  write_r_num,
  input  write_en,
  input  clk,
  input  [31:0] read2_r_num,
  output [31:0] read1_data,
  output [31:0] read2_data
);

  wire and_1_out;
  wire [31:0] R20_q;

  and and_1 (and_1_out, write_r_num, write_en);
  Register #(.width(32)) R20 (.D(write_data), .en(and_1_out), .Q(R20_q), .clk(clk));  // open: clr
  assign read1_data = read1_r_num & R20_q;  // AND_Gate and_2, 32 bits wide
  assign read2_data = R20_q & read2_r_num;  // AND_Gate and_3, 32 bits wide
endmodule

module R21 (
  input  [31:0] read1_r_num,
  input  [31:0] write_data,
  input  write_r_num,
  input  write_en,
  input  clk,
  input  [31:0] read2_r_num,
  output [31:0] read1_data,
  output [31:0] read2_data
);

  wire and_1_out;
  wire [31:0] R21_q;

  and and_1 (and_1_out, write_r_num, write_en);
  Register #(.width(32)) R21 (.D(write_data), .en(and_1_out), .Q(R21_q), .clk(clk));  // open: clr
  assign read1_data = read1_r_num & R21_q;  // AND_Gate and_2, 32 bits wide
  assign read2_data = R21_q & read2_r_num;  // AND_Gate and_3, 32 bits wide
endmodule

module R22 (
  input  [31:0] read1_r_num,
  input  [31:0] write_data,
  input  write_r_num,
  input  write_en,
  input  clk,
  input  [31:0] read2_r_num,
  output [31:0] read1_data,
  output [31:0] read2_data
);

  wire and_1_out;
  wire [31:0] R22_q;

  and and_1 (and_1_out, write_r_num, write_en);
  Register #(.width(32)) R22 (.D(write_data), .en(and_1_out), .Q(R22_q), .clk(clk));  // open: clr
  assign read1_data = read1_r_num & R22_q;  // AND_Gate and_2, 32 bits wide
  assign read2_data = R22_q & read2_r_num;  // AND_Gate and_3, 32 bits wide
endmodule

module R23 (
  input  [31:0] read1_r_num,
  input  [31:0] write_data,
  input  write_r_num,
  input  write_en,
  input  clk,
  input  [31:0] read2_r_num,
  output [31:0] read1_data,
  output [31:0] read2_data
);

  wire and_1_out;
  wire [31:0] R23_q;

  and and_1 (and_1_out, write_r_num, write_en);
  Register #(.width(32)) R23 (.D(write_data), .en(and_1_out), .Q(R23_q), .clk(clk));  // open: clr
  assign read1_data = read1_r_num & R23_q;  // AND_Gate and_2, 32 bits wide
  assign read2_data = R23_q & read2_r_num;  // AND_Gate and_3, 32 bits wide
endmodule

module R24 (
  input  [31:0] read1_r_num,
  input  [31:0] write_data,
  input  write_r_num,
  input  write_en,
  input  clk,
  input  [31:0] read2_r_num,
  output [31:0] read1_data,
  output [31:0] read2_data
);

  wire and_1_out;
  wire [31:0] R24_q;

  and and_1 (and_1_out, write_r_num, write_en);
  Register #(.width(32)) R24 (.D(write_data), .en(and_1_out), .Q(R24_q), .clk(clk));  // open: clr
  assign read1_data = read1_r_num & R24_q;  // AND_Gate and_2, 32 bits wide
  assign read2_data = R24_q & read2_r_num;  // AND_Gate and_3, 32 bits wide
endmodule

module R25 (
  input  [31:0] read1_r_num,
  input  [31:0] write_data,
  input  write_r_num,
  input  write_en,
  input  clk,
  input  [31:0] read2_r_num,
  output [31:0] read1_data,
  output [31:0] read2_data
);

  wire and_1_out;
  wire [31:0] R25_q;

  and and_1 (and_1_out, write_r_num, write_en);
  Register #(.width(32)) R25 (.D(write_data), .en(and_1_out), .Q(R25_q), .clk(clk));  // open: clr
  assign read1_data = read1_r_num & R25_q;  // AND_Gate and_2, 32 bits wide
  assign read2_data = R25_q & read2_r_num;  // AND_Gate and_3, 32 bits wide
endmodule

module R26 (
  input  [31:0] read1_r_num,
  input  [31:0] write_data,
  input  write_r_num,
  input  write_en,
  input  clk,
  input  [31:0] read2_r_num,
  output [31:0] read1_data,
  output [31:0] read2_data
);

  wire and_1_out;
  wire [31:0] R26_q;

  and and_1 (and_1_out, write_r_num, write_en);
  Register #(.width(32)) R26 (.D(write_data), .en(and_1_out), .Q(R26_q), .clk(clk));  // open: clr
  assign read1_data = read1_r_num & R26_q;  // AND_Gate and_2, 32 bits wide
  assign read2_data = R26_q & read2_r_num;  // AND_Gate and_3, 32 bits wide
endmodule

module R27 (
  input  [31:0] read1_r_num,
  input  [31:0] write_data,
  input  write_r_num,
  input  write_en,
  input  clk,
  input  [31:0] read2_r_num,
  output [31:0] read1_data,
  output [31:0] read2_data
);

  wire and_1_out;
  wire [31:0] R27_q;

  and and_1 (and_1_out, write_r_num, write_en);
  Register #(.width(32)) R27 (.D(write_data), .en(and_1_out), .Q(R27_q), .clk(clk));  // open: clr
  assign read1_data = read1_r_num & R27_q;  // AND_Gate and_2, 32 bits wide
  assign read2_data = R27_q & read2_r_num;  // AND_Gate and_3, 32 bits wide
endmodule

module R28 (
  input  [31:0] read1_r_num,
  input  [31:0] write_data,
  input  write_r_num,
  input  write_en,
  input  clk,
  input  [31:0] read2_r_num,
  output [31:0] read1_data,
  output [31:0] read2_data
);

  wire and_1_out;
  wire [31:0] R28_q;

  and and_1 (and_1_out, write_r_num, write_en);
  Register #(.width(32)) R28 (.D(write_data), .en(and_1_out), .Q(R28_q), .clk(clk));  // open: clr
  assign read1_data = read1_r_num & R28_q;  // AND_Gate and_2, 32 bits wide
  assign read2_data = R28_q & read2_r_num;  // AND_Gate and_3, 32 bits wide
endmodule

module R29 (
  input  [31:0] read1_r_num,
  input  [31:0] write_data,
  input  write_r_num,
  input  write_en,
  input  clk,
  input  [31:0] read2_r_num,
  output [31:0] read1_data,
  output [31:0] out,
  output [31:0] read2_data
);

  wire and_1_out;

  and and_1 (and_1_out, write_r_num, write_en);
  Register #(.width(32)) R29 (.D(write_data), .en(and_1_out), .Q(out), .clk(clk));  // open: clr
  assign read1_data = read1_r_num & out;  // AND_Gate and_2, 32 bits wide
  assign read2_data = out & read2_r_num;  // AND_Gate and_3, 32 bits wide
endmodule

module R30 (
  input  [31:0] read1_r_num,
  input  [31:0] write_data,
  input  write_r_num,
  input  write_en,
  input  clk,
  input  [31:0] read2_r_num,
  output [31:0] read1_data,
  output [31:0] read2_data
);

  wire and_1_out;
  wire [31:0] R30_q;

  and and_1 (and_1_out, write_r_num, write_en);
  Register #(.width(32)) R30 (.D(write_data), .en(and_1_out), .Q(R30_q), .clk(clk));  // open: clr
  assign read1_data = read1_r_num & R30_q;  // AND_Gate and_2, 32 bits wide
  assign read2_data = R30_q & read2_r_num;  // AND_Gate and_3, 32 bits wide
endmodule

module R31 (
  input  [31:0] read1_r_num,
  input  [31:0] write_data,
  input  write_r_num,
  input  write_en,
  input  clk,
  input  [31:0] read2_r_num,
  output [31:0] read1_data,
  output [31:0] out,
  output [31:0] read2_data
);

  wire and_1_out;

  and and_1 (and_1_out, write_r_num, write_en);
  Register #(.width(32)) R31 (.D(write_data), .en(and_1_out), .Q(out), .clk(clk));  // open: clr
  assign read1_data = read1_r_num & out;  // AND_Gate and_2, 32 bits wide
  assign read2_data = out & read2_r_num;  // AND_Gate and_3, 32 bits wide
endmodule
