// Logisim project alu.circ as structural Verilog: 10 circuits, main circuit main
module main (
  input  [31:0] X,
  input  [31:0] Y,
  input  [3:0] Switch,
  output Signed_Overflow,
  output Equal,
  output [31:0] Result
);

  wire addOverflow_overflow, subOverflow_overflow;
  wire [31:0] adder_1_out, and_1_out, or_1_out, sll_1_out, slt_1_out, sltu_1_out, sra_1_out, srl_1_out,
       subtractor_1_out;

  Comparator #(.width(32)) comparator_1 (.a(X), .b(Y), .eq(Equal));  // open: gt, lt
  sll sll_1 (.Y(Y), .X(X), .out(sll_1_out));
  srl srl_1 (.Y(Y), .X(X), .out(srl_1_out));
  sra sra_1 (.Y(Y), .X(X), .out(sra_1_out));
  Adder #(.width(32)) adder_1 (.a(X), .b(Y), .out(adder_1_out));  // open: cin, cout
  Subtractor #(.width(32)) subtractor_1 (.a(X), .b(Y), .out(subtractor_1_out));  // open: bin, bout
  addOverflow addOverflow (.X(X), .Y(Y), .result(Result), .overflow(addOverflow_overflow));
  subOverflow subOverflow (.X(X), .Y(Y), .result(Result), .overflow(subOverflow_overflow));
  \and  and_1 (.X(X), .Y(Y), .out(and_1_out));
  \or  or_1 (.X(X), .Y(Y), .out(or_1_out));
  slt slt_1 (.X(X), .Y(Y), .out(slt_1_out));
  sltu sltu_1 (.X(X), .Y(Y), .out(sltu_1_out));
  Multiplexer #(.select(4), .width(32), .enable("false")) multiplexer_1 (
    .in0(sll_1_out), .in1(srl_1_out), .in2(sra_1_out), .in5(adder_1_out), .in6(adder_1_out),
    .in7(subtractor_1_out), .in8(subtractor_1_out), .in9(and_1_out), .in10(or_1_out), .in14(slt_1_out),
    .in15(sltu_1_out), .out(Result), .sel(Switch));  // open: in3, in4, in11, in12, in13
  Multiplexer #(.select(4), .enable("false")) multiplexer_2 (
    .in0(1'b0), .in1(1'b0), .in2(1'b0), .in5(addOverflow_overflow), .in6(1'b0), .in7(subOverflow_overflow),
    .in8(1'b0), .in9(1'b0), .in10(1'b0), .in14(1'b0), .in15(1'b0), .out(Signed_Overflow), .sel(Switch));  // open: in3, in4, in11, in12, in13

  // Other names for the same wires on the sheet: overflow = Signed_Overflow; S[3:0] = Switch

  // Notes on the sheet:
  //   INPUTS to your circuit
  //   DON'T CHANGE THE LOCATIONS OF THE INPUTS AND OUTPUTS!
  //   OUTPUTS from your circuit
endmodule

module \and  (
  input  [31:0] X,
  input  [31:0] Y,
  output [31:0] out
);

  assign out = X & Y;  // AND_Gate and_1, 32 bits wide
endmodule

module \or  (
  input  [31:0] X,
  input  [31:0] Y,
  output [31:0] out
);

  assign out = X | Y;  // OR_Gate or_1, 32 bits wide
endmodule

module slt (
  input  [31:0] X,
  input  [31:0] Y,
  output [31:0] out
);

  Comparator #(.width(32)) comparator_1 (.a(X), .b(Y), .lt(out[0]));  // open: gt, eq

  assign out[31:1] = {31{1'b0}};
endmodule

module sltu (
  input  [31:0] X,
  input  [31:0] Y,
  output [31:0] out
);

  wire and_1_out, and_2_out, comparator_1_eq, comparator_1_lt, comparator_2_lt, not_1_out, not_2_out;

  Comparator #(.width(32)) comparator_1 (
    .a({1'b0, X[31:1]}), .b({1'b0, Y[31:1]}), .eq(comparator_1_eq), .lt(comparator_1_lt));  // open: gt
  and and_1 (and_1_out, X[0], comparator_1_eq);
  and and_2 (and_2_out, comparator_1_eq, Y[0]);
  not not_1 (not_1_out, and_1_out);
  Comparator #(.width(1)) comparator_2 (.a(not_1_out), .b(not_2_out), .lt(comparator_2_lt));  // open: gt, eq
  not not_2 (not_2_out, and_2_out);
  or or_1 (out[0], comparator_2_lt, comparator_1_lt);

  assign out[31:1] = {31{1'b0}};
endmodule

module addOverflow (
  input  [31:0] X,
  input  [31:0] Y,
  input  [31:0] result,
  output overflow
);

  wire and_1_out, and_2_out, not_1_out, not_2_out, not_3_out;

  not not_1 (not_1_out, X[31]);
  not not_2 (not_2_out, Y[31]);
  and and_1 (and_1_out, not_1_out, not_2_out, result[31]);
  and and_2 (and_2_out, X[31], Y[31], not_3_out);
  not not_3 (not_3_out, result[31]);
  or or_1 (overflow, and_1_out, and_2_out);
endmodule

module subOverflow (
  input  [31:0] X,
  input  [31:0] Y,
  input  [31:0] result,
  output overflow
);

  wire and_1_out, and_2_out, not_1_out, not_2_out, not_3_out;

  not not_1 (not_1_out, X[31]);
  and and_1 (and_1_out, not_1_out, Y[31], result[31]);
  not not_2 (not_2_out, Y[31]);
  and and_2 (and_2_out, X[31], not_2_out, not_3_out);
  not not_3 (not_3_out, result[31]);
  or or_1 (overflow, and_1_out, and_2_out);
endmodule

module sll (
  input  [31:0] Y,
  input  [31:0] X,
  output [31:0] out
);

  Shifter #(.width(32)) shifter_1 (.in(Y), .\dist (X[4:0]), .out(out));
endmodule

module srl (
  input  [31:0] Y,
  input  [31:0] X,
  output [31:0] out
);

  Shifter #(.width(32), .shift("lr")) shifter_1 (.in(Y), .\dist (X[4:0]), .out(out));
endmodule

module sra (
  input  [31:0] Y,
  input  [31:0] X,
  output [31:0] out
);

  Shifter #(.width(32), .shift("ar")) shifter_1 (.in(Y), .\dist (X[4:0]), .out(out));
endmodule
