// Logisim project cpu.circ as structural Verilog: 3 circuits, main circuit main
module main (
  input  [31:0] INSTRUCTION,
  input  CLOCK,
  output [31:0] FETCH_ADDRESS,
  output [31:0] s0_Value,
  output [31:0] s1_Value,
  output [31:0] s2_Value,
  output [31:0] ra_Value,
  output [31:0] sp_Value
);

  wire ALUSrc, and_4_out, beq, bltzal, bne, Branch, comparator_2_eq, comparator_3_eq, comparator_4_eq,
       comparator_5_lt, equal, jal, jr, Jump, lui, MemToReg, MemWrite, or_1_out, RegDst, RegWrite;
  wire [2:0] ALUOp;
  wire [3:0] ALUSwitch;
  wire [4:0] multiplexer_2_out, multiplexer_3_out;
  wire [25:0] shifter_1_out;
  wire [31:0] adder_1_out, adder_2_out, imm32, main_1_read_data_2, main_2_result, main_3_result, main_4_p5,
       multiplexer_1_out, multiplexer_4_out, multiplexer_5_out, multiplexer_6_out, multiplexer_7_out,
       multiplexer_8_out, multiplexer_9_out, rs_data, shifter_2_out;

  MainControl maincontrol_1 (
    .funct(INSTRUCTION[5:0]), .opcode(INSTRUCTION[31:26]), .RegWrite(RegWrite), .RegDst(RegDst),
    .ALUSrc(ALUSrc), .ALUOp(ALUOp), .Jump(Jump), .MemToReg(MemToReg), .MemWrite(MemWrite), .Branch(Branch));
  ALUControl ALU_Control (.funct(INSTRUCTION[5:0]), .ALUOp(ALUOp), .ALUSwitch(ALUSwitch));
  Comparator #(.width(6)) comparator_1 (.a(INSTRUCTION[5:0]), .b(6'b001000), .eq(jr));  // open: gt, lt
  assign imm32 = {{16{INSTRUCTION[15]}}, INSTRUCTION[15:0]};  // Bit_Extender bit_extender_1
  Comparator #(.width(6)) comparator_2 (.a(INSTRUCTION[31:26]), .b(6'b000100), .eq(comparator_2_eq));  // open: gt, lt
  Comparator #(.width(6)) comparator_3 (.a(INSTRUCTION[31:26]), .b(6'b000101), .eq(comparator_3_eq));  // open: gt, lt
  Comparator #(.width(6)) comparator_4 (.a(INSTRUCTION[31:26]), .b(6'b000001), .eq(comparator_4_eq));  // open: gt, lt
  Comparator #(.width(32)) comparator_5 (.a(rs_data), .b({32{1'b0}}), .lt(comparator_5_lt));  // open: gt, eq
  Comparator #(.width(6)) comparator_6 (.a(INSTRUCTION[31:26]), .b(6'b000011), .eq(jal));  // open: gt, lt
  Comparator #(.width(6)) comparator_7 (.a(INSTRUCTION[31:26]), .b(6'b001111), .eq(lui));  // open: gt, lt
  and and_1 (beq, comparator_2_eq, equal);
  and and_2 (bne, comparator_3_eq, ~equal);  // AND_Gate
  and and_3 (bltzal, comparator_4_eq, comparator_5_lt);
  Multiplexer #(.width(32), .enable("false")) multiplexer_1 (
    .in0(multiplexer_8_out), .in1(rs_data), .out(multiplexer_1_out), .sel(jr));
  Multiplexer #(.width(5), .enable("false")) multiplexer_2 (
    .in0(INSTRUCTION[20:16]), .in1(INSTRUCTION[15:11]), .out(multiplexer_2_out), .sel(RegDst));
  Register #(.width(32)) PC (.D(multiplexer_1_out), .en(1'b1), .Q(FETCH_ADDRESS), .clk(CLOCK));  // open: clr
  Multiplexer #(.width(5), .enable("false")) multiplexer_3 (
    .in0(multiplexer_2_out), .in1({5{1'b1}}), .out(multiplexer_3_out), .sel(jal));
  Adder #(.width(32)) adder_1 (.a(32'h4), .b(FETCH_ADDRESS), .out(adder_1_out));  // open: cin, cout
  regfile_main main_1 (
    .Read_Register_1(INSTRUCTION[25:21]), .Read_Register_2(INSTRUCTION[20:16]),
    .Write_Register(multiplexer_3_out), .Write_Data(multiplexer_4_out), .Write_Enable(RegWrite),
    .Clock(CLOCK), .Read_Data_1(rs_data), .Read_Data_2(main_1_read_data_2), .s0_Value(s0_Value),
    .s1_Value(s1_Value), .s2_Value(s2_Value), .ra_Value(ra_Value), .sp_Value(sp_Value));
  Multiplexer #(.width(32), .enable("false")) multiplexer_4 (
    .in0(multiplexer_5_out), .in1(adder_2_out), .out(multiplexer_4_out), .sel(jal));
  Shifter #(.width(26)) shifter_1 (.in(INSTRUCTION[25:0]), .\dist (5'b00010), .out(shifter_1_out));
  Multiplexer #(.width(32), .enable("false")) multiplexer_5 (
    .in0(multiplexer_9_out), .in1({INSTRUCTION[15:0], {16{1'b0}}}), .out(multiplexer_5_out), .sel(lui));
  Adder #(.width(32)) adder_2 (.a(32'h4), .b(FETCH_ADDRESS), .out(adder_2_out));  // open: cin, cout
  Shifter #(.width(32)) shifter_2 (.in(imm32), .\dist (5'b00010), .out(shifter_2_out));
  alu_main main_2 (
    .Switch(4'b0101), .X(adder_1_out), .Result(main_2_result), .Y(shifter_2_out));  // open: Equal, Signed_Overflow
  alu_main main_3 (
    .Switch(ALUSwitch), .X(rs_data), .Equal(equal), .Result(main_3_result), .Y(multiplexer_6_out));  // open: Signed_Overflow
  Multiplexer #(.width(32), .enable("false")) multiplexer_6 (
    .in0(main_1_read_data_2), .in1(imm32), .out(multiplexer_6_out), .sel(ALUSrc));
  and and_4 (and_4_out, Branch, or_1_out);
  or or_1 (or_1_out, beq, bltzal, bne);
  Multiplexer #(.width(32), .enable("false")) multiplexer_7 (
    .in0(adder_1_out), .in1(main_2_result), .out(multiplexer_7_out), .sel(and_4_out));
  // mem_main main_4: pin names not known; wires that end beside it: main_3_result, main_1_read_data_2, MemWrite, CLOCK, main_4_p5
  Multiplexer #(.width(32), .enable("false")) multiplexer_8 (
    .in0(multiplexer_7_out), .in1({adder_1_out[31:28], shifter_1_out, 2'b00}), .out(multiplexer_8_out),
    .sel(Jump));
  Multiplexer #(.width(32), .enable("false")) multiplexer_9 (
    .in0(main_3_result), .in1(main_4_p5), .out(multiplexer_9_out), .sel(MemToReg));

  // Other names for the same wires on the sheet: address[25:0] = INSTRUCTION[25:0]; funct[5:0] = INSTRUCTION[5:0];
  //   imm[15:0] = INSTRUCTION[15:0]; rd[4:0] = INSTRUCTION[15:11]; clk = CLOCK; fetch_addr[31:0] = FETCH_ADDRESS;
  //   rt[4:0] = INSTRUCTION[20:16]; rs[4:0] = INSTRUCTION[25:21]; opcode[5:0] = INSTRUCTION[31:26];
  //   ra[31:0] = ra_Value; s0[31:0] = s0_Value; s1[31:0] = s1_Value; s2[31:0] = s2_Value; sp[31:0] = sp_Value

  // Notes on the sheet:
  //   Output
  //   These are outputs/inputs from run.circ
  //   Inputs
  //   These are DEBUG/TEST outputs from your circuit.
endmodule

module MainControl (
  input  [5:0] funct,
  input  [5:0] opcode,
  output RegWrite,
  output RegDst,
  output ALUSrc,
  output [2:0] ALUOp,
  output Jump,
  output MemToReg,
  output MemWrite,
  output Branch
);

  wire addi, addiu, andi, beq, bltzal, bne, j, jal, jr, lui, nor_3_out, or_3_out, ori, slti, sltiu;

  Comparator #(.width(6)) comparator_1 (.a(funct), .b(6'b001000), .eq(jr));  // open: gt, lt
  Comparator #(.width(6)) comparator_2 (.a(opcode), .b({6{1'b0}}), .eq(RegDst));  // open: gt, lt
  Comparator #(.width(6)) comparator_3 (.a(opcode), .b(6'b001000), .eq(addi));  // open: gt, lt
  Comparator #(.width(6)) comparator_4 (.a(opcode), .b(6'b001001), .eq(addiu));  // open: gt, lt
  Comparator #(.width(6), .mode("unsigned")) comparator_5 (.a(opcode), .b(6'b000010), .eq(j));  // open: gt, lt
  Comparator #(.width(6), .mode("unsigned")) comparator_6 (.a(opcode), .b(6'b000011), .eq(jal));  // open: gt, lt
  Comparator #(.width(6)) comparator_7 (.a(opcode), .b(6'b001010), .eq(slti));  // open: gt, lt
  Comparator #(.width(6)) comparator_8 (.a(opcode), .b(6'b001011), .eq(sltiu));  // open: gt, lt
  Comparator #(.width(6)) comparator_9 (.a(opcode), .b(6'b001100), .eq(andi));  // open: gt, lt
  Comparator #(.width(6)) comparator_10 (.a(opcode), .b(6'b001101), .eq(ori));  // open: gt, lt
  Comparator #(.width(6)) comparator_11 (.a(opcode), .b(6'b001111), .eq(lui));  // open: gt, lt
  Comparator #(.width(6)) comparator_12 (.a(opcode), .b(6'b100011), .eq(MemToReg));  // open: gt, lt
  Comparator #(.width(6)) comparator_13 (.a(opcode), .b(6'b101011), .eq(MemWrite));  // open: gt, lt
  Comparator #(.width(6)) comparator_14 (.a(opcode), .b(6'b000100), .eq(beq));  // open: gt, lt
  Comparator #(.width(6)) comparator_15 (.a(opcode), .b(6'b000101), .eq(bne));  // open: gt, lt
  Comparator #(.width(6)) comparator_16 (.a(opcode), .b(6'b000001), .eq(bltzal));  // open: gt, lt
  or or_1 (Jump, j, jal);
  nor nor_1 (ALUSrc, beq, RegDst, bne);
  or or_2 (Branch, beq, bne, bltzal);
  nor nor_2 (RegWrite, j, MemWrite, beq, bne, jr);
  or or_3 (or_3_out, MemToReg, addiu, MemWrite);
  assign ALUOp = RegDst ? 3'b111 : 3'bz;  // Controlled_Buffer controlled_buffer_1
  assign ALUOp = addi ? 3'b001 : 3'bz;  // Controlled_Buffer controlled_buffer_2
  assign ALUOp = or_3_out ? 3'b010 : 3'bz;  // Controlled_Buffer controlled_buffer_3
  assign ALUOp = andi ? 3'b011 : 3'bz;  // Controlled_Buffer controlled_buffer_4
  assign ALUOp = ori ? 3'b100 : 3'bz;  // Controlled_Buffer controlled_buffer_5
  assign ALUOp = slti ? 3'b101 : 3'bz;  // Controlled_Buffer controlled_buffer_6
  assign ALUOp = sltiu ? 3'b110 : 3'bz;  // Controlled_Buffer controlled_buffer_7
  assign ALUOp = nor_3_out ? 3'b000 : 3'bz;  // Controlled_Buffer controlled_buffer_8
  nor nor_3 (nor_3_out, RegDst, addi, addiu, andi, ori, slti, sltiu);

  // Other names for the same wires on the sheet: lw = MemToReg; R_type = RegDst; sw = MemWrite

  // Notes on the sheet:
  //   noop: 000
  //   addOp: 001
  //   adduOp: 010
  //   andOp: 011
  //   orOp:100
  //   sltOp: 101
  //   sltuOp: 110
  //   R-type: 111
endmodule

module ALUControl (
  input  [5:0] funct,
  input  [2:0] ALUOp,
  output [3:0] ALUSwitch
);

  wire add, addOp, addu, adduOp, \and , and_1_out, and_2_out, and_3_out, and_4_out, and_5_out, andOp, noop,
       \or , or_1_out, or_2_out, or_3_out, or_4_out, or_5_out, or_6_out, orOp, R_type, sll, slt, sltOp, sltu,
       sltuOp, sra, srl, sub, subu;

  Comparator #(.width(6)) comparator_1 (.a(funct), .b({6{1'b0}}), .eq(sll));  // open: gt, lt
  Comparator #(.width(6)) comparator_2 (.a(funct), .b(6'b000010), .eq(srl));  // open: gt, lt
  Comparator #(.width(6)) comparator_3 (.a(funct), .b(6'b000011), .eq(sra));  // open: gt, lt
  Comparator #(.width(6)) comparator_4 (.a(funct), .b(6'b100000), .eq(add));  // open: gt, lt
  Comparator #(.width(6)) comparator_5 (.a(funct), .b(6'b100001), .eq(addu));  // open: gt, lt
  Comparator #(.width(6)) comparator_6 (.a(funct), .b(6'b100010), .eq(sub));  // open: gt, lt
  Comparator #(.width(6)) comparator_7 (.a(funct), .b(6'b100011), .eq(subu));  // open: gt, lt
  Comparator #(.width(6)) comparator_8 (.a(funct), .b(6'b100100), .eq(\and ));  // open: gt, lt
  Comparator #(.width(6)) comparator_9 (.a(funct), .b(6'b100101), .eq(\or ));  // open: gt, lt
  Comparator #(.width(6)) comparator_10 (.a(funct), .b(6'b101010), .eq(slt));  // open: gt, lt
  Comparator #(.width(6)) comparator_11 (.a(funct), .b(6'b101011), .eq(sltu));  // open: gt, lt
  Decoder #(.select(3), .enable("false")) decoder_1 (
    .out0(noop), .out1(addOp), .out2(adduOp), .out3(andOp), .out4(orOp), .out5(sltOp), .out6(sltuOp),
    .out7(R_type), .sel(ALUOp));
  and and_1 (and_1_out, sll, R_type);
  and and_2 (and_2_out, srl, R_type);
  and and_3 (and_3_out, sra, R_type);
  or or_1 (or_1_out, add, addOp);
  or or_2 (or_2_out, addu, adduOp);
  and and_4 (and_4_out, sub, R_type);
  and and_5 (and_5_out, subu, R_type);
  or or_3 (or_3_out, \and , andOp);
  or or_4 (or_4_out, \or , orOp);
  or or_5 (or_5_out, slt, sltOp);
  or or_6 (or_6_out, sltu, sltuOp);
  assign ALUSwitch = and_1_out ? 4'b0000 : 4'bz;  // Controlled_Buffer controlled_buffer_1
  assign ALUSwitch = and_2_out ? 4'b0001 : 4'bz;  // Controlled_Buffer controlled_buffer_2
  assign ALUSwitch = and_3_out ? 4'b0010 : 4'bz;  // Controlled_Buffer controlled_buffer_3
  assign ALUSwitch = or_1_out ? 4'b0101 : 4'bz;  // Controlled_Buffer controlled_buffer_4
  assign ALUSwitch = or_2_out ? 4'b0110 : 4'bz;  // Controlled_Buffer controlled_buffer_5
  assign ALUSwitch = and_4_out ? 4'b0111 : 4'bz;  // Controlled_Buffer controlled_buffer_6
  assign ALUSwitch = and_5_out ? 4'b0111 : 4'bz;  // Controlled_Buffer controlled_buffer_7
  assign ALUSwitch = or_3_out ? 4'b1001 : 4'bz;  // Controlled_Buffer controlled_buffer_8
  assign ALUSwitch = or_4_out ? 4'b1010 : 4'bz;  // Controlled_Buffer controlled_buffer_9
  assign ALUSwitch = or_5_out ? 4'b1110 : 4'bz;  // Controlled_Buffer controlled_buffer_10
  assign ALUSwitch = or_6_out ? 4'b1111 : 4'bz;  // Controlled_Buffer controlled_buffer_11
endmodule
